# Fritzing sketch Demokit (saved by Fritzing 0.7.4b)
breadboards: 1

parts:
  LED1 = RGB LED - (4 legs) [package="5 mm [THT]"]
  J1 = Basic Servo
  R1 = Resistor [tolerance=±5% resistance=330 package="0603 [SMD]"]
  R3 = Resistor [tolerance=±5% resistance=330 package="0603 [SMD]"]
  R7 = Resistor [tolerance=±5% resistance=330 package="0603 [SMD]"]
  S1 = Pushbutton [package="[THT]"]
  Arduino1 = Arduino

nets:
  N1: LED1.red_cathode, R1.Pin_1
  VCC: LED1.common_anode, J1.vcc, Arduino1.+5V
  N2: LED1.green_cathode, R3.Pin_1
  N3: LED1.blue_cathode, R7.Pin_1
  GND: J1.gnd, S1.Pin_3, S1.Pin_4, Arduino1.GND
  N4: J1.pulse, Arduino1.D9
  N5: R1.Pin_0, Arduino1.D6
  N6: R3.Pin_0, Arduino1.D5
  N7: R7.Pin_0, Arduino1.D3
  N8: S1.Pin_1, S1.Pin_2, Arduino1.A4
