# Fritzing sketch MyRCCar (saved by Fritzing 0.6.4b)
breadboards: 1

parts:
  Arduino1 = Arduino
  Direction = Basic Servo
  Moteur = Basic Servo
  S1 = Round Pushbutton
  S2 = Round Pushbutton

nets:
  GND: Arduino1.GND, Direction.gnd, Moteur.gnd, S1.leg1, S2.leg1
  N1: Arduino1.D12, Direction.pulse
  N2: Arduino1.D10, Moteur.pulse
  N3: Arduino1.D3, S1.leg0
  N4: Arduino1.D2, S2.leg0
  VCC: Arduino1.+5V, Direction.vcc, Moteur.vcc
